// Logisim project smart room project.circ as structural Verilog: 1 circuit, main circuit main
module main (
  input  Light,
  input  Fan,
  input  AC,
  input  Entry,
  input  Exit,
  input  Reset,
  output AC_2,
  output Fan_2,
  output Light_2,
  output Full,
  output Entry_door,
  output Empty,
  output Exit_door
);

  wire and_1_out, and_2_out, and_3_out, and_4_out, and_5_out, and_6_out, and_7_out, and_8_out, and_9_out,
       clock_1_out, d_ff_1_q, d_ff_1_qn, d_ff_2_q, d_ff_2_qn, not_1_out, not_2_out, not_3_out, or_1_out,
       or_2_out;

  Clock clock_1 (.out(clock_1_out));
  D_Flip_Flop d_ff_1 (
    .clk(clock_1_out), .D(or_1_out), .Q(d_ff_1_q), .Qn(d_ff_1_qn), .reset(Reset));  // open: preset, en
  D_Flip_Flop d_ff_2 (
    .clk(clock_1_out), .D(or_2_out), .Q(d_ff_2_q), .Qn(d_ff_2_qn), .reset(Reset));  // open: preset, en
  not not_1 (not_1_out, Entry);
  not not_2 (not_2_out, Exit);
  and and_1 (and_1_out, d_ff_1_q, d_ff_2_q);
  and and_2 (and_2_out, d_ff_1_q, Entry);
  and and_3 (and_3_out, d_ff_2_q, Entry, not_2_out);
  and and_4 (and_4_out, d_ff_1_q, not_2_out);
  and and_5 (and_5_out, not_2_out, not_1_out, d_ff_2_q);
  and and_6 (and_6_out, Exit, Entry, d_ff_2_q);
  and and_7 (and_7_out, d_ff_2_q, Entry, d_ff_1_q);
  and and_8 (and_8_out, d_ff_2_qn, Entry, not_2_out);
  and and_9 (and_9_out, Exit, not_1_out, d_ff_2_qn, d_ff_1_q);
  and and_10 (Full, d_ff_1_q, d_ff_2_q);
  and and_11 (Empty, d_ff_1_qn, d_ff_2_qn);
  not not_3 (not_3_out, Empty);
  or or_1 (or_1_out, and_1_out, and_2_out, and_3_out, and_4_out);
  or or_2 (or_2_out, and_5_out, and_6_out, and_7_out, and_8_out, and_9_out);
  not not_4 (Entry_door, Full);
  not not_5 (Exit_door, Empty);
  and and_12 (AC_2, AC, not_3_out);
  and and_13 (Fan_2, Fan, not_3_out);
  and and_14 (Light_2, Light, not_3_out);

  // Notes on the sheet:
  //   Clock
  //   Inputs:
  //   |
  //   \/
  //   Inputs:
  //   Outputs:
  //   (1: accessible, 0: locked)
  //   (1: accessible, 0: locked)
endmodule
